# Fritzing sketch sensor-node.bmp085-dht11 (saved by Fritzing 0.9.5d)
circuit board: 5.35384cm x 5.38549cm
perfboards: 1

parts:
  元件2 = Arduino Pro Mini (5V)
  元件3 = Barometric Pressure Sensor - BMP085 Breakout
  U1 = LM3480IM4 [package=sot23-3]
  元件4 = NRF24L01+ Breakout Board
  DHT1 = DHT11 Humitidy and Temperature Sensor
  J1 = male pin header, 4 pins [form="♂ (male)"]
  R1 = Resistor [tolerance=±5% resistance=300k package="0805 [SMD]"]
  R2 = Resistor [tolerance=±5% resistance=910k package="0805 [SMD]"]

nets:
  GND: 元件2.GND, 元件3.GND, U1.GND, 元件4.GND, DHT1.GND, J1.pin2, R1.Pin_0
  N1: 元件2.A4, 元件3.SDA
  N2: 元件2.A5, 元件3.SCL
  6V: 元件2.RAW, J1.pin1, R2.Pin_1
  5V: 元件2.VCC, 元件3.VCC, U1.IN, DHT1.VDD
  N3: 元件2.A0, R1.Pin_1, R2.Pin_0
  N4: 元件2.SCK, 元件4.SCK
  N5: 元件2.MISO, 元件4.MISO
  N6: 元件2.MOSI, 元件4.MOSI
  N7: 元件2.D10, 元件4.CS
  N8: 元件2.D9, 元件4.CE
  N9: 元件2.D3, DHT1.DATA
  N10: 元件2.D2, 元件4.IRQ
  N11: 元件2.RXI, J1.pin3
  N12: 元件2.TXO, J1.pin4
  3.3V: U1.OUT, 元件4.VCC

custom parts:
  DHT11 Humitidy and Temperature Sensor: DHT11 Humidity and Temperature Sensor
